// Logisim project Encoder.circ as structural Verilog: 2 circuits, main circuit main
module main (
  input  D0,
  input  D1,
  input  D2,
  input  D3,
  input  EI,
  output EO,
  output [1:0] out_7,
  output out_8
);

  Priority_Encoder #(.select(2)) priority_encoder_1 (
    .in0(D0), .in1(D1), .in2(D2), .in3(D3), .out(out_7), .gs(out_8), .en_out(EO), .en_in(EI));
endmodule

module FourBitSample (
  input  D3,
  input  D2,
  input  D1,
  input  D0,
  output x,
  output y,
  output v
);

  wire and_1_out, not_1_out;

  not not_1 (not_1_out, D2);
  or or_1 (x, D3, D2);
  and and_1 (and_1_out, not_1_out, D1);
  or or_2 (y, and_1_out, D3);
  or or_3 (v, x, D1, D0);
endmodule
