// Logisim project MultiplexerProjecy.circ as structural Verilog: 1 circuit, main circuit main
module main (
  input  in_1,
  input  in_2,
  input  in_3,
  input  in_4,
  input  [1:0] in_5,
  input  in_6,
  output out_7
);

  Multiplexer #(.enable("true"), .select(2)) multiplexer_1 (
    .in0(in_1), .in1(in_2), .in2(in_3), .in3(in_4), .out(out_7), .sel(in_5), .en(in_6));
endmodule
