// Logisim project RippleAdder.circ as structural Verilog: 4 circuits, main circuit main
module main (
  input  [3:0] A,
  input  [3:0] B,
  output V,
  output C,
  output Z,
  output N,
  output [3:0] out_7
);

  wire AH0_carry_out, AH1_carry_out, AH2_carry_out, and_1_out, or_1_out, or_2_out, xor_2_out;

  FullAdder AH3 (.carry_in(AH2_carry_out), .x(B[3]), .y(A[3]), .carry_out(C), .sum(N));
  FullAdder AH2 (.carry_in(AH1_carry_out), .x(B[2]), .y(A[2]), .carry_out(AH2_carry_out), .sum(out_7[2]));
  FullAdder AH1 (.carry_in(AH0_carry_out), .x(B[1]), .y(A[1]), .carry_out(AH1_carry_out), .sum(out_7[1]));
  FullAdder AH0 (.carry_in(1'b0), .x(B[0]), .y(A[0]), .carry_out(AH0_carry_out), .sum(out_7[0]));
  or or_1 (or_1_out, B[3], A[3]);
  nor nor_1 (Z, out_7[0], out_7[1], out_7[2], N);
  and and_1 (and_1_out, B[3], A[3]);
  or or_2 (or_2_out, out_7[2], or_1_out);
  xor xor_1 (V, or_2_out, xor_2_out);
  xor xor_2 (xor_2_out, and_1_out, out_7[2]);

  assign out_7[3] = N;
endmodule

module HalfAdder (
  input  x,
  input  y,
  output sum,
  output carry
);

  xor xor_1 (sum, x, y);
  and and_1 (carry, x, y);
endmodule

module FullAdder (
  input  carry_in,
  input  x,
  input  y,
  output carry_out,
  output sum
);

  wire HA1_carry, HA1_sum, HA2_carry;

  HalfAdder HA1 (.x(x), .y(y), .sum(HA1_sum), .carry(HA1_carry));
  HalfAdder HA2 (.x(carry_in), .y(HA1_sum), .sum(sum), .carry(HA2_carry));
  or or_1 (carry_out, HA1_carry, HA2_carry);
endmodule

module AdderSubtractor (
  input  [3:0] in_1,
  input  [3:0] in_2
);

  main main_1 (.A(in_1), .B(in_2));  // open: V, C, Z, N, out_7
endmodule
